// Logisim project single_cycle_processor.circ as structural Verilog
module main (
  input  debug_open_seg,
  output [11:0] debug_I_imm,
  output [4:0] debug_a2,
  output [31:0] debug_WD3,
  output [4:0] debug_a1,
  output [4:0] debug_a3
);

  wire branch_1_pcsrc, clock_1_out, control_unit_1_memtoreg, control_unit_1_memwrite, control_unit_1_pcsrc,
       control_unit_1_regwrite, control_unit_1_seg, or_1_out;
  wire [1:0] control_unit_1_alusrc, control_unit_1_branch;
  wire [2:0] alu_1_cmpresult, control_unit_1_aluctrl, instr_mem_1_funct3_14_12;
  wire [3:0] register_2_q, register_2_q_2, register_2_q_3, register_2_q_4, register_2_q_6;
  wire [6:0] instr_mem_1_funct7_31_25, instr_mem_1_opcode;
  wire [11:0] instr_mem_1_s_imm_b_imm;
  wire [27:16] register_2_q_5;
  wire [31:0] \_12位到32位补码扩展_pcsrc , \_12到32位补码扩展_pcsrc , adder_1_out, alu_1_aluresult, alusrc_srcb,
       data_mem_1_rd, multiplexer_1_out, pcplus1_1_pc_1, reg_file_1_rd1, reg_file_1_rd2, register_1_q;

  Multiplexer #(.width(32), .enable("false")) multiplexer_1 (
    .in0(pcplus1_1_pc_1), .in1(adder_1_out), .out(multiplexer_1_out), .sel(branch_1_pcsrc));
  Register #(.width(32), .trigger("falling")) register_1 (
    .D(multiplexer_1_out), .Q(register_1_q), .clk(clock_1_out));  // open: en, clr
  Clock clock_1 (.out(clock_1_out));
  instr_mem instr_mem_1 (
    .PC(register_1_q), .funct7_31_25(instr_mem_1_funct7_31_25), .rs2_24_20(debug_a2), .rs1_19_15(debug_a1),
    .funct3_14_12(instr_mem_1_funct3_14_12), .rd_11_7(debug_a3), .opcode(instr_mem_1_opcode),
    .clk(clock_1_out), .I_imm(debug_I_imm), .S_imm_B_imm(instr_mem_1_s_imm_b_imm));
  pcplus1 pcplus1_1 (.pc(register_1_q), .PC_1(pcplus1_1_pc_1));
  control_unit control_unit_1 (
    .opcode(instr_mem_1_opcode), .funct7(instr_mem_1_funct7_31_25), .funct3(instr_mem_1_funct3_14_12),
    .regwrite(control_unit_1_regwrite), .alusrc(control_unit_1_alusrc), .aluctrl(control_unit_1_aluctrl),
    .memtoreg(control_unit_1_memtoreg), .seg(control_unit_1_seg), .memwrite(control_unit_1_memwrite),
    .branch(control_unit_1_branch), .pcsrc(control_unit_1_pcsrc));
  reg_file reg_file_1 (
    .A1(debug_a1), .WD3(debug_WD3), .A3(debug_a3), .A2(debug_a2), .rd1(reg_file_1_rd1), .rd2(reg_file_1_rd2),
    .WE3(control_unit_1_regwrite), .clk(clock_1_out));
  _12to32sign_extend \_12位到32位补码扩展  (.alusrcop(debug_I_imm), .pcsrc(\_12位到32位补码扩展_pcsrc ));
  _12to32sign_extend \_12到32位补码扩展  (.alusrcop(instr_mem_1_s_imm_b_imm), .pcsrc(\_12到32位补码扩展_pcsrc ));
  or or_1 (or_1_out, debug_open_seg, control_unit_1_seg);
  alusrc alusrc (
    .rd2(reg_file_1_rd2), .I_imm(\_12位到32位补码扩展_pcsrc ), .S_imm(\_12到32位补码扩展_pcsrc ),
    .alusrcop(control_unit_1_alusrc), .srcB(alusrc_srcb));
  Adder #(.width(32)) adder_1 (.a(\_12到32位补码扩展_pcsrc ), .b(pcplus1_1_pc_1), .out(adder_1_out));  // open: cin, cout
  Hex_Digit_Display hex_digit_display_1 (.value(register_2_q_6));  // open: dp
  Hex_Digit_Display hex_digit_display_2 (.value(register_2_q_5[27:24]));  // open: dp
  Register #(.width(32), .trigger("high")) register_2 (
    .D(reg_file_1_rd1),
    .Q({register_2_q_6, register_2_q_5, register_2_q_4, register_2_q_3, register_2_q_2, register_2_q}),
    .clk(or_1_out));  // open: en, clr
  alu alu_1 (
    .srcA(reg_file_1_rd1), .srcB(alusrc_srcb), .aluctrl(control_unit_1_aluctrl), .aluResult(alu_1_aluresult),
    .cmpResult(alu_1_cmpresult));
  Hex_Digit_Display hex_digit_display_3 (.value(register_2_q_5[23:20]));  // open: dp
  Hex_Digit_Display hex_digit_display_4 (.value(register_2_q_5[19:16]));  // open: dp
  data_mem data_mem_1 (
    .A(alu_1_aluresult), .WD(reg_file_1_rd2), .we(control_unit_1_memwrite), .clk(clock_1_out),
    .rd(data_mem_1_rd));
  Hex_Digit_Display hex_digit_display_5 (.value(register_2_q_3));  // open: dp
  Hex_Digit_Display hex_digit_display_6 (.value(register_2_q_4));  // open: dp
  branch branch_1 (
    .pcsrcop(control_unit_1_pcsrc), .branch(control_unit_1_branch), .alucmpsrc(alu_1_cmpresult),
    .pcsrc(branch_1_pcsrc));
  Hex_Digit_Display hex_digit_display_7 (.value(register_2_q_2));  // open: dp
  Multiplexer #(.width(32), .enable("false")) multiplexer_2 (
    .in0(alu_1_aluresult), .in1(data_mem_1_rd), .out(debug_WD3), .sel(control_unit_1_memtoreg));
  Hex_Digit_Display hex_digit_display_8 (.value(register_2_q));  // open: dp

  // Notes on the sheet:
  //   pc
  //   pcsrc
  //   指令存储器
  //   pc+1
  //   控制单元(译码)
  //   寄存器堆
  //   pc+立即数
  //   alu
  //   数据存储器
  //   branch
endmodule

module instr_mem (
  input  clk,
  input  [31:0] PC,
  output [6:0] funct7_31_25,
  output [4:0] rs2_24_20,
  output [4:0] rs1_19_15,
  output [2:0] funct3_14_12,
  output [4:0] rd_11_7,
  output [6:0] opcode,
  output [11:0] I_imm,
  output [11:0] S_imm_B_imm
);

  wire [9:0] bit_extender_1_out;
  wire [31:0] rom_1_data;

  Bit_Extender #(.in_width(32), .out_width(10)) bit_extender_1 (.in(PC), .out(bit_extender_1_out));
  ROM #(.addrWidth(10), .dataWidth(32)) rom_1 (.addr(bit_extender_1_out), .data(rom_1_data), .sel(1'b1));
  assign {funct7_31_25, I_imm[4:0], rs1_19_15, funct3_14_12, rd_11_7, opcode} = clk ? rom_1_data : 32'bz;  // Controlled_Buffer controlled_buffer_1

  assign I_imm[11:5] = funct7_31_25;
  assign rs2_24_20 = I_imm[4:0];
  assign S_imm_B_imm = {funct7_31_25, rd_11_7};

  // Notes on the sheet:
  //   contents of rom_1 (hex, n*v repeats v):
  //   200093 300113 22081b3 302223 402083 8000
endmodule

module reg_file (
  input  clk,
  input  [4:0] A1,
  input  WE3,
  input  [31:0] WD3,
  input  [4:0] A3,
  input  [4:0] A2,
  output [31:0] rd1,
  output [31:0] rd2
);

  wire and_1_out, and_2_out, and_3_out, and_4_out, and_5_out, and_6_out, and_7_out, and_8_out, and_9_out,
       and_10_out, and_11_out, and_12_out, and_13_out, and_14_out, and_15_out, and_16_out, and_17_out,
       and_18_out, and_19_out, and_20_out, and_21_out, and_22_out, and_23_out, and_24_out, and_25_out,
       and_26_out, and_27_out, and_28_out, and_29_out, and_30_out, and_31_out, and_32_out, decoder_1_out0,
       decoder_1_out1, decoder_1_out2, decoder_1_out3, decoder_1_out4, decoder_1_out5, decoder_1_out6,
       decoder_1_out7, decoder_1_out8, decoder_1_out9, decoder_1_out10, decoder_1_out11, decoder_1_out12,
       decoder_1_out13, decoder_1_out14, decoder_1_out15, decoder_1_out16, decoder_1_out17, decoder_1_out18,
       decoder_1_out19, decoder_1_out20, decoder_1_out21, decoder_1_out22, decoder_1_out23, decoder_1_out24,
       decoder_1_out25, decoder_1_out26, decoder_1_out27, decoder_1_out28, decoder_1_out29, decoder_1_out30,
       decoder_1_out31;
  wire [31:0] register_1_q, register_2_q, register_3_q, register_4_q, register_5_q, register_6_q,
       register_7_q, register_8_q, register_9_q, register_10_q, register_11_q, register_12_q, register_13_q,
       register_14_q, register_15_q, register_16_q, register_17_q, register_18_q, register_19_q,
       register_20_q, register_21_q, register_22_q, register_23_q, register_24_q, register_25_q,
       register_26_q, register_27_q, register_28_q, register_29_q, register_30_q, register_31_q,
       register_32_q;

  Decoder #(.select(5), .enable("false")) decoder_1 (
    .out0(decoder_1_out0), .out1(decoder_1_out1), .out2(decoder_1_out2), .out3(decoder_1_out3),
    .out4(decoder_1_out4), .out5(decoder_1_out5), .out6(decoder_1_out6), .out7(decoder_1_out7),
    .out8(decoder_1_out8), .out9(decoder_1_out9), .out10(decoder_1_out10), .out11(decoder_1_out11),
    .out12(decoder_1_out12), .out13(decoder_1_out13), .out14(decoder_1_out14), .out15(decoder_1_out15),
    .out16(decoder_1_out16), .out17(decoder_1_out17), .out18(decoder_1_out18), .out19(decoder_1_out19),
    .out20(decoder_1_out20), .out21(decoder_1_out21), .out22(decoder_1_out22), .out23(decoder_1_out23),
    .out24(decoder_1_out24), .out25(decoder_1_out25), .out26(decoder_1_out26), .out27(decoder_1_out27),
    .out28(decoder_1_out28), .out29(decoder_1_out29), .out30(decoder_1_out30), .out31(decoder_1_out31),
    .sel(A3));
  and and_1 (and_1_out, decoder_1_out0, 1'b0);
  and and_2 (and_2_out, decoder_1_out1, WE3);
  and and_3 (and_3_out, decoder_1_out2, WE3);
  and and_4 (and_4_out, decoder_1_out3, WE3);
  and and_5 (and_5_out, decoder_1_out4, WE3);
  and and_6 (and_6_out, decoder_1_out5, WE3);
  and and_7 (and_7_out, decoder_1_out6, WE3);
  and and_8 (and_8_out, decoder_1_out7, WE3);
  and and_9 (and_9_out, decoder_1_out8, WE3);
  and and_10 (and_10_out, decoder_1_out9, WE3);
  and and_11 (and_11_out, decoder_1_out10, WE3);
  and and_12 (and_12_out, decoder_1_out11, WE3);
  and and_13 (and_13_out, decoder_1_out12, WE3);
  and and_14 (and_14_out, decoder_1_out13, WE3);
  and and_15 (and_15_out, decoder_1_out14, WE3);
  and and_16 (and_16_out, decoder_1_out15, WE3);
  and and_17 (and_17_out, decoder_1_out16, WE3);
  and and_18 (and_18_out, decoder_1_out17, WE3);
  and and_19 (and_19_out, decoder_1_out18, WE3);
  and and_20 (and_20_out, decoder_1_out19, WE3);
  and and_21 (and_21_out, decoder_1_out20, WE3);
  and and_22 (and_22_out, decoder_1_out21, WE3);
  and and_23 (and_23_out, decoder_1_out22, WE3);
  and and_24 (and_24_out, decoder_1_out23, WE3);
  and and_25 (and_25_out, decoder_1_out24, WE3);
  and and_26 (and_26_out, decoder_1_out25, WE3);
  and and_27 (and_27_out, decoder_1_out26, WE3);
  and and_28 (and_28_out, decoder_1_out27, WE3);
  and and_29 (and_29_out, decoder_1_out28, WE3);
  and and_30 (and_30_out, decoder_1_out29, WE3);
  and and_31 (and_31_out, decoder_1_out30, WE3);
  and and_32 (and_32_out, decoder_1_out31, WE3);
  Register #(.width(32), .trigger("falling")) register_1 (
    .D(WD3), .en(and_1_out), .Q(register_1_q), .clk(clk));  // open: clr
  Register #(.width(32), .trigger("falling")) register_2 (
    .D(WD3), .en(and_2_out), .Q(register_2_q), .clk(clk));  // open: clr
  Register #(.width(32), .trigger("falling")) register_3 (
    .D(WD3), .en(and_3_out), .Q(register_3_q), .clk(clk));  // open: clr
  Register #(.width(32), .trigger("falling")) register_4 (
    .D(WD3), .en(and_4_out), .Q(register_4_q), .clk(clk));  // open: clr
  Register #(.width(32), .trigger("falling")) register_5 (
    .D(WD3), .en(and_5_out), .Q(register_5_q), .clk(clk));  // open: clr
  Register #(.width(32), .trigger("falling")) register_6 (
    .D(WD3), .en(and_6_out), .Q(register_6_q), .clk(clk));  // open: clr
  Register #(.width(32), .trigger("falling")) register_7 (
    .D(WD3), .en(and_7_out), .Q(register_7_q), .clk(clk));  // open: clr
  Register #(.width(32), .trigger("falling")) register_8 (
    .D(WD3), .en(and_8_out), .Q(register_8_q), .clk(clk));  // open: clr
  Register #(.width(32), .trigger("falling")) register_9 (
    .D(WD3), .en(and_9_out), .Q(register_9_q), .clk(clk));  // open: clr
  Register #(.width(32), .trigger("falling")) register_10 (
    .D(WD3), .en(and_10_out), .Q(register_10_q), .clk(clk));  // open: clr
  Register #(.width(32), .trigger("falling")) register_11 (
    .D(WD3), .en(and_11_out), .Q(register_11_q), .clk(clk));  // open: clr
  Register #(.width(32), .trigger("falling")) register_12 (
    .D(WD3), .en(and_12_out), .Q(register_12_q), .clk(clk));  // open: clr
  Register #(.width(32), .trigger("falling")) register_13 (
    .D(WD3), .en(and_13_out), .Q(register_13_q), .clk(clk));  // open: clr
  Register #(.width(32), .trigger("falling")) register_14 (
    .D(WD3), .en(and_14_out), .Q(register_14_q), .clk(clk));  // open: clr
  Register #(.width(32), .trigger("falling")) register_15 (
    .D(WD3), .en(and_15_out), .Q(register_15_q), .clk(clk));  // open: clr
  Register #(.width(32), .trigger("falling")) register_16 (
    .D(WD3), .en(and_16_out), .Q(register_16_q), .clk(clk));  // open: clr
  Register #(.width(32), .trigger("falling")) register_17 (
    .D(WD3), .en(and_17_out), .Q(register_17_q), .clk(clk));  // open: clr
  Register #(.width(32), .trigger("falling")) register_18 (
    .D(WD3), .en(and_18_out), .Q(register_18_q), .clk(clk));  // open: clr
  Register #(.width(32), .trigger("falling")) register_19 (
    .D(WD3), .en(and_19_out), .Q(register_19_q), .clk(clk));  // open: clr
  Register #(.width(32), .trigger("falling")) register_20 (
    .D(WD3), .en(and_20_out), .Q(register_20_q), .clk(clk));  // open: clr
  Register #(.width(32), .trigger("falling")) register_21 (
    .D(WD3), .en(and_21_out), .Q(register_21_q), .clk(clk));  // open: clr
  Register #(.width(32), .trigger("falling")) register_22 (
    .D(WD3), .en(and_22_out), .Q(register_22_q), .clk(clk));  // open: clr
  Register #(.width(32), .trigger("falling")) register_23 (
    .D(WD3), .en(and_23_out), .Q(register_23_q), .clk(clk));  // open: clr
  Register #(.width(32), .trigger("falling")) register_24 (
    .D(WD3), .en(and_24_out), .Q(register_24_q), .clk(clk));  // open: clr
  Register #(.width(32), .trigger("falling")) register_25 (
    .D(WD3), .en(and_25_out), .Q(register_25_q), .clk(clk));  // open: clr
  Register #(.width(32), .trigger("falling")) register_26 (
    .D(WD3), .en(and_26_out), .Q(register_26_q), .clk(clk));  // open: clr
  Register #(.width(32), .trigger("falling")) register_27 (
    .D(WD3), .en(and_27_out), .Q(register_27_q), .clk(clk));  // open: clr
  Register #(.width(32), .trigger("falling")) register_28 (
    .D(WD3), .en(and_28_out), .Q(register_28_q), .clk(clk));  // open: clr
  Register #(.width(32), .trigger("falling")) register_29 (
    .D(WD3), .en(and_29_out), .Q(register_29_q), .clk(clk));  // open: clr
  Register #(.width(32), .trigger("falling")) register_30 (
    .D(WD3), .en(and_30_out), .Q(register_30_q), .clk(clk));  // open: clr
  Register #(.width(32), .trigger("falling")) register_31 (
    .D(WD3), .en(and_31_out), .Q(register_31_q), .clk(clk));  // open: clr
  Register #(.width(32), .trigger("falling")) register_32 (
    .D(WD3), .en(and_32_out), .Q(register_32_q), .clk(clk));  // open: clr
  Multiplexer #(.select(5), .width(32), .enable("false")) multiplexer_1 (
    .in0(register_1_q), .in1(register_2_q), .in2(register_3_q), .in3(register_4_q), .in4(register_5_q),
    .in5(register_6_q), .in6(register_7_q), .in7(register_8_q), .in8(register_9_q), .in9(register_10_q),
    .in10(register_11_q), .in11(register_12_q), .in12(register_13_q), .in13(register_14_q),
    .in14(register_15_q), .in15(register_16_q), .in16(register_17_q), .in17(register_18_q),
    .in18(register_19_q), .in19(register_20_q), .in20(register_21_q), .in21(register_22_q),
    .in22(register_23_q), .in23(register_24_q), .in24(register_25_q), .in25(register_26_q),
    .in26(register_27_q), .in27(register_28_q), .in28(register_29_q), .in29(register_30_q),
    .in30(register_31_q), .in31(register_32_q), .out(rd1), .sel(A1));
  Multiplexer #(.select(5), .width(32), .enable("false")) multiplexer_2 (
    .in0(register_1_q), .in1(register_2_q), .in2(register_3_q), .in3(register_4_q), .in4(register_5_q),
    .in5(register_6_q), .in6(register_7_q), .in7(register_8_q), .in8(register_9_q), .in9(register_10_q),
    .in10(register_11_q), .in11(register_12_q), .in12(register_13_q), .in13(register_14_q),
    .in14(register_15_q), .in15(register_16_q), .in16(register_17_q), .in17(register_18_q),
    .in18(register_19_q), .in19(register_20_q), .in20(register_21_q), .in21(register_22_q),
    .in22(register_23_q), .in23(register_24_q), .in24(register_25_q), .in25(register_26_q),
    .in26(register_27_q), .in27(register_28_q), .in28(register_29_q), .in29(register_30_q),
    .in30(register_31_q), .in31(register_32_q), .out(rd2), .sel(A2));
endmodule

module alu (
  input  [2:0] aluctrl,
  input  [31:0] srcA,
  input  [31:0] srcB,
  output [31:0] aluResult,
  output [2:0] cmpResult
);

  wire nor_1_out;
  wire [2:0] comparator_1_lt;
  wire [31:0] adder_1_out, multiplier_1_out, subtractor_1_out;

  Adder #(.width(32)) adder_1 (.a(srcA), .b(srcB), .out(adder_1_out));  // open: cin, cout
  nor nor_1 (nor_1_out, aluctrl[0], aluctrl[1], aluctrl[2]);
  assign aluResult = nor_1_out ? adder_1_out : 32'bz;  // Controlled_Buffer controlled_buffer_1
  Multiplier #(.width(32)) multiplier_1 (.a(srcA), .b(srcB), .out(multiplier_1_out));  // open: cin, cout
  assign aluResult = aluctrl[0] ? multiplier_1_out : 32'bz;  // Controlled_Buffer controlled_buffer_2
  assign aluResult = aluctrl[1] ? subtractor_1_out : 32'bz;  // Controlled_Buffer controlled_buffer_3
  Subtractor #(.width(32)) subtractor_1 (.a(srcA), .b(srcB), .out(subtractor_1_out));  // open: bin, bout
  Comparator #(.width(32)) comparator_1 (
    .a(srcA), .b(srcB), .gt(comparator_1_lt[2]), .eq(comparator_1_lt[1]), .lt(comparator_1_lt[0]));
  assign cmpResult = aluctrl[2] ? comparator_1_lt : 3'bz;  // Controlled_Buffer controlled_buffer_4
endmodule

module data_mem (
  input  [31:0] A,
  input  [31:0] WD,
  input  we,
  input  clk,
  output [31:0] rd
);

  wire not_1_out;
  wire [9:0] bit_extender_1_out;

  Bit_Extender #(.in_width(32), .out_width(10)) bit_extender_1 (.in(A), .out(bit_extender_1_out));
  not not_1 (not_1_out, clk);
  RAM #(.addrWidth(10), .dataWidth(32), .bus("separate")) ram_1 (
    .addr(bit_extender_1_out), .din(WD), .data(rd), .str(we), .sel(1'b1), .clk(not_1_out), .ld(1'b1));  // open: clr
endmodule

module control_unit (
  input  [6:0] opcode,
  input  [6:0] funct7,
  input  [2:0] funct3,
  output regwrite,
  output [1:0] alusrc,
  output [2:0] aluctrl,
  output memtoreg,
  output seg,
  output memwrite,
  output [1:0] branch,
  output pcsrc
);

  ctrl_regwrite ctrl_regwrite_1 (
    .op6(opcode[6]), .op5(opcode[5]), .op4(opcode[4]), .op3(opcode[3]), .op2(opcode[2]), .op1(opcode[1]),
    .op0(opcode[0]), .regwrite(regwrite));
  ctrl_alusrc ctrl_alusrc_1 (
    .op6(opcode[6]), .op5(opcode[5]), .op4(opcode[4]), .op3(opcode[3]), .op2(opcode[2]), .op1(opcode[1]),
    .op0(opcode[0]), .alusrc1(alusrc[1]), .alusrc0(alusrc[0]));
  ctrl_aluctrl ctrl_aluctrl_1 (.opcode(opcode), .funct7(funct7), .out_3(aluctrl));
  ctrl_memtoreg ctrl_memtoreg_1 (
    .op6(opcode[6]), .op5(opcode[5]), .op4(opcode[4]), .op3(opcode[3]), .op2(opcode[2]), .op1(opcode[1]),
    .op0(opcode[0]), .memtoreg(memtoreg));
  nor nor_1 (seg, opcode[6], opcode[5], opcode[4], opcode[3], opcode[2], opcode[1], opcode[0]);
  Comparator #(.width(7)) comparator_1 (.a(opcode), .b(7'b0100011), .eq(memwrite));  // open: gt, lt
  Comparator #(.width(7)) comparator_2 (.a(opcode), .b(7'b1100011), .eq(pcsrc));  // open: gt, lt

  assign branch = {funct3[2], funct3[0]};
endmodule

module ctrl_regwrite (
  input  op6,
  input  op5,
  input  op4,
  input  op3,
  input  op2,
  input  op1,
  input  op0,
  output regwrite
);

  wire and_1_out, and_2_out, and_3_out, not_1_out, not_2_out, not_3_out, not_4_out, not_5_out, not_6_out,
       not_7_out, not_8_out;

  not not_1 (not_1_out, op6);
  not not_2 (not_2_out, op5);
  not not_3 (not_3_out, op3);
  not not_4 (not_4_out, op2);
  not not_5 (not_5_out, op6);
  not not_6 (not_6_out, op3);
  not not_7 (not_7_out, op2);
  not not_8 (not_8_out, op4);
  and and_1 (and_1_out, not_1_out, not_2_out, not_3_out, not_4_out, op1, op0);
  and and_2 (and_2_out, not_5_out, op4, not_6_out, not_7_out, op1, op0);
  and and_3 (and_3_out, op6, op5, not_8_out, op3, op2, op1, op0);
  or or_1 (regwrite, and_1_out, and_2_out, and_3_out);
endmodule

module ctrl_aluctrl (
  input  [6:0] opcode,
  input  [6:0] funct7,
  output [2:0] out_3
);

  wire comparator_1_eq, comparator_2_eq, comparator_3_eq, comparator_4_eq, or_1_out;
  wire [2:0] bit_extender_1_out;

  Bit_Extender #(.in_width(7), .out_width(3)) bit_extender_1 (.in(funct7), .out(bit_extender_1_out));
  Comparator #(.width(7)) comparator_1 (.a(7'b0110011), .b(opcode), .eq(comparator_1_eq));  // open: gt, lt
  Comparator #(.width(7)) comparator_2 (.a(7'b0010011), .b(opcode), .eq(comparator_2_eq));  // open: gt, lt
  Comparator #(.width(7)) comparator_3 (.a(7'b0100011), .b(opcode), .eq(comparator_3_eq));  // open: gt, lt
  Comparator #(.width(7)) comparator_4 (.a(opcode), .b(7'b1100011), .eq(comparator_4_eq));  // open: gt, lt
  assign out_3 = comparator_1_eq ? bit_extender_1_out : 3'bz;  // Controlled_Buffer controlled_buffer_1
  or or_1 (or_1_out, comparator_2_eq, comparator_3_eq);
  assign out_3 = comparator_4_eq ? 3'b100 : 3'bz;  // Controlled_Buffer controlled_buffer_2
  assign out_3 = or_1_out ? 3'b000 : 3'bz;  // Controlled_Buffer controlled_buffer_3

  // Notes on the sheet:
  //   R op
  //   I op
  //   S op
  //   B op
endmodule

module ctrl_memtoreg (
  input  op6,
  input  op5,
  input  op4,
  input  op3,
  input  op2,
  input  op1,
  input  op0,
  output memtoreg
);

  wire not_1_out, not_2_out, not_3_out, not_4_out, not_5_out;

  not not_1 (not_1_out, op6);
  not not_2 (not_2_out, op5);
  not not_3 (not_3_out, op4);
  not not_4 (not_4_out, op3);
  not not_5 (not_5_out, op2);
  and and_1 (memtoreg, not_1_out, not_2_out, not_3_out, not_4_out, not_5_out, op1, op0);
endmodule

module pcplus1 (
  input  [31:0] pc,
  output [31:0] PC_1
);

  Adder #(.width(32)) adder_1 (.a(pc), .b(32'h1), .out(PC_1));  // open: cin, cout
endmodule

module ctrl_alusrc (
  input  op6,
  input  op5,
  input  op4,
  input  op3,
  input  op2,
  input  op1,
  input  op0,
  output alusrc1,
  output alusrc0
);

  wire not_1_out, not_2_out, not_3_out, not_4_out, not_5_out, not_6_out, not_7_out, not_8_out;

  not not_1 (not_1_out, op6);
  not not_2 (not_2_out, op4);
  not not_3 (not_3_out, op3);
  not not_4 (not_4_out, op2);
  not not_5 (not_5_out, op6);
  not not_6 (not_6_out, op5);
  not not_7 (not_7_out, op3);
  not not_8 (not_8_out, op2);
  and and_1 (alusrc1, not_1_out, op5, not_2_out, not_3_out, not_4_out, op1, op0);
  and and_2 (alusrc0, not_5_out, not_6_out, op4, not_7_out, not_8_out, op1, op0);
endmodule

module alusrc (
  input  [1:0] alusrcop,
  input  [31:0] rd2,
  input  [31:0] I_imm,
  input  [31:0] S_imm,
  output [31:0] srcB
);

  Multiplexer #(.select(2), .width(32), .enable("false")) multiplexer_1 (
    .in0(rd2), .in1(I_imm), .in2(S_imm), .out(srcB), .sel(alusrcop));  // open: in3
endmodule

module branch (
  input  pcsrcop,
  input  [1:0] branch,
  input  [2:0] alucmpsrc,
  output pcsrc
);

  wire and_1_out, and_2_out, and_3_out, and_4_out, and_5_out, not_1_out, not_2_out, not_3_out, not_4_out,
       not_5_out, not_6_out, not_7_out, not_8_out, not_9_out, not_10_out, not_11_out, not_12_out, not_13_out,
       not_14_out;

  not not_1 (not_1_out, branch[1]);
  not not_2 (not_2_out, branch[0]);
  not not_3 (not_3_out, alucmpsrc[2]);
  not not_4 (not_4_out, alucmpsrc[0]);
  not not_5 (not_5_out, branch[1]);
  not not_6 (not_6_out, alucmpsrc[2]);
  not not_7 (not_7_out, alucmpsrc[1]);
  not not_8 (not_8_out, alucmpsrc[1]);
  not not_9 (not_9_out, alucmpsrc[0]);
  not not_10 (not_10_out, branch[0]);
  not not_11 (not_11_out, alucmpsrc[2]);
  not not_12 (not_12_out, alucmpsrc[1]);
  not not_13 (not_13_out, alucmpsrc[2]);
  not not_14 (not_14_out, alucmpsrc[0]);
  and and_1 (and_1_out, pcsrcop, not_1_out, not_2_out, not_3_out, alucmpsrc[1], not_4_out);
  and and_2 (and_2_out, pcsrcop, not_5_out, branch[0], not_6_out, not_7_out, alucmpsrc[0]);
  and and_3 (and_3_out, pcsrcop, branch[0], alucmpsrc[2], not_8_out, not_9_out);
  and and_4 (and_4_out, pcsrcop, branch[1], not_10_out, not_11_out, not_12_out, alucmpsrc[0]);
  and and_5 (and_5_out, pcsrcop, branch[1], branch[0], not_13_out, alucmpsrc[1], not_14_out);
  or or_1 (pcsrc, and_1_out, and_2_out, and_3_out, and_4_out, and_5_out);
endmodule

module _12to32sign_extend (
  input  [11:0] alusrcop,
  output [31:0] pcsrc
);

  assign pcsrc = {{20{alusrcop[11]}}, alusrcop};  // Bit_Extender bit_extender_1
endmodule
